# Fritzing sketch candy-machine (saved by Fritzing 0.9.1b)

parts:
  Raspberry_Pi_A1 = Raspberry Pi A
  U1 = G3VM-61E1 [package=g3vm-61e1]
  M2 = DC Motor

nets:
  N1: Raspberry_Pi_A1.5V, U1.P$1, U1.P$6
  N2: Raspberry_Pi_A1.GND, M2.pin_1
  N3: Raspberry_Pi_A1.GPIO_4, U1.P$5
  N4: U1.P$2, M2.pin_2
